# Fritzing sketch FleeCar_Schematic (saved by Fritzing 0.9.3b)
breadboards: 1

parts:
  U2 = atmega328 [package=dip]
  IC2 = L293D [package=THT]
  IC3 = L293D [package=THT]
  R1 = Resistor [tolerance=±5% resistance=220 package=THT]
  C1 = Ceramic Capacitor [capacitance=100nF package="100 mil [THT, multilayer]"]
  M1 = DC Motor
  M2 = DC Motor
  M3 = DC Motor
  M4 = DC Motor
  BeagleBone1 = BeagleBone Black
  U3 = atmega328 [package=dip]
  R2 = Resistor [tolerance=±5% resistance=220 package=THT]
  C2 = Ceramic Capacitor [capacitance=100nF package="100 mil [THT, multilayer]"]
  Part2 = Adafruit 4-channel I2C-safe Bi-directional Logic Level Converter [part_number="Adafruit #757"]
  J1 = Infrared Proximity Sensor
  J2 = Infrared Proximity Sensor
  Power_plug1 = Power plug

nets:
  N1: U2.RESET, R1.Pin_1
  N2: U2.D4, IC2.In_4
  VCC: U2.VCC, U2.AVCC, U2.AREF, IC2.+V, IC3.+V, R1.Pin_0, C1.0, BeagleBone1.no_name_yet#5, U3.VCC, U3.AVCC, U3.AREF, R2.Pin_0, C2.0, Part2.HV, J1.Vcc, J2.Vcc
  GND: U2.GND, IC2.0V, IC3.0V, C1.1, BeagleBone1.no_name_yet#1, U3.GND, C2.1, Part2.GND, J1.GND, J2.GND
  N3: U2.XLAT1, IC2.In_1
  N4: U2.XLAT2, IC2.In_2
  N5: U2.D6_(PWM), IC2.Enable_1, IC2.Enable_2, IC3.Enable_1, IC3.Enable_2
  N6: U2.D7, IC3.In_1
  N7: U2.D8, IC3.In_2
  N8: U2.D9_(PWM), IC2.In_3
  N9: U2.D10_(PWM), BeagleBone1.no_name_yet#17
  N10: U2.D11_(PWM), BeagleBone1.no_name_yet#18
  N11: U2.D12, Part2.B1
  N12: U2.D13, BeagleBone1.no_name_yet#22
  N13: U2.A0, IC3.In_3
  N14: U2.A1, IC3.In_4
  N15: IC2.Out_1_(_Controlled_by_Enable_1_), M3.pin_2
  N16: IC2.Out_2_(_Controlled_by_Enable_1_), M3.pin_1
  N17: IC2.+Vmotor, IC3.+Vmotor, Power_plug1.VCC
  N18: IC2.Out_3_(_Controlled_by_Enable_2_), M1.pin_2
  N19: IC2.Out_4_(_Controlled_by_Enable_2_), M1.pin_1
  N20: IC3.Out_1_(_Controlled_by_Enable_1_), M4.pin_2
  N21: IC3.Out_2_(_Controlled_by_Enable_1_), M4.pin_1
  N22: IC3.Out_3_(_Controlled_by_Enable_2_), M2.pin_2
  N23: IC3.Out_4_(_Controlled_by_Enable_2_), M2.pin_1
  N24: BeagleBone1.no_name_yet#3, Part2.LV
  N25: BeagleBone1.no_name_yet#21, BeagleBone1.no_name_yet#26, Part2.A1
  N26: BeagleBone1.no_name_yet#28, U3.D10_(PWM)
  N27: BeagleBone1.no_name_yet#29, Part2.A2
  N28: BeagleBone1.no_name_yet#30, U3.D11_(PWM)
  N29: BeagleBone1.no_name_yet#31, U3.D13
  N30: U3.RESET, R2.Pin_1
  N31: U3.D12, Part2.B2
  N32: U3.A0, J2.Vout
  N33: U3.A1, J1.Vout

custom parts:
  BeagleBone Black: BeagleBone Black rev. A5B
  Adafruit 4-channel I2C-safe Bi-directional Logic Level Converter: Because the Arduino (and Basic Stamp) are 5V devices, and most modern sensors, displays, flash cards and modes are 3.3V-only, many makers find that they need to perform level shifting/conversion to protect the 3.3V device from 5V. We do have some other handy level shifters in the shop, from the DIP 74LVC245 to the fancy bi-directional TXB0108. However, neither of these are happy to work with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
